// Logisim project circuit.circ as structural Verilog: 6 circuits, main circuit pin_slice
module pin_slice (
  input  zi,
  input  ci,
  input  qi,
  input  wi,
  output wo,
  output co,
  output qo,
  output zo
);

  wire and_1_out;

  D_Flip_Flop d_ff_1 (.clk(ci), .D(qi), .Q(qo));  // open: Qn, preset, en, reset
  or or_1 (zo, zi, and_1_out);
  and and_1 (and_1_out, qo, wi);

  assign co = ci;
  assign wo = wi;
endmodule

module pin (
  input  PSI,
  input  W0,
  input  W1,
  input  W2,
  input  PCLK,
  output Z0,
  output Z1,
  output Z2
);

  wire pin_slice_1_co, pin_slice_1_qo, pin_slice_1_zo, pin_slice_2_co, pin_slice_2_qo, pin_slice_2_wo,
       pin_slice_2_zo, pin_slice_3_co, pin_slice_3_qo, pin_slice_3_wo, pin_slice_3_zo, pin_slice_4_co,
       pin_slice_4_qo, pin_slice_4_zo, pin_slice_6_co, pin_slice_6_qo, pin_slice_6_wo, pin_slice_7_co,
       pin_slice_7_qo, pin_slice_7_wo, pin_slice_7_zo, pin_slice_8_co, pin_slice_8_qo, pin_slice_8_wo,
       pin_slice_8_zo, pin_slice_9_co, pin_slice_9_qo, pin_slice_9_wo;

  pin_slice pin_slice_1 (
    .ci(pin_slice_6_co), .qi(pin_slice_6_qo), .zo(pin_slice_1_zo), .wi(pin_slice_2_wo), .zi(1'b0),
    .co(pin_slice_1_co), .qo(pin_slice_1_qo));  // open: wo
  pin_slice pin_slice_2 (
    .ci(pin_slice_9_co), .qi(pin_slice_9_qo), .zo(pin_slice_2_zo), .wi(pin_slice_3_wo), .zi(1'b0),
    .co(pin_slice_2_co), .qo(pin_slice_2_qo), .wo(pin_slice_2_wo));
  pin_slice pin_slice_3 (
    .ci(PCLK), .qi(PSI), .zo(pin_slice_3_zo), .wi(W0), .zi(1'b0), .co(pin_slice_3_co), .qo(pin_slice_3_qo),
    .wo(pin_slice_3_wo));
  pin_slice pin_slice_4 (
    .ci(pin_slice_1_co), .qi(pin_slice_1_qo), .zo(pin_slice_4_zo), .wi(pin_slice_7_wo), .zi(pin_slice_1_zo),
    .co(pin_slice_4_co), .qo(pin_slice_4_qo));  // open: wo
  pin_slice pin_slice_5 (
    .ci(pin_slice_4_co), .qi(pin_slice_4_qo), .zo(Z0), .wi(pin_slice_6_wo), .zi(pin_slice_4_zo));  // open: co, qo, wo
  pin_slice pin_slice_6 (
    .ci(pin_slice_7_co), .qi(pin_slice_7_qo), .zo(Z1), .wi(pin_slice_9_wo), .zi(pin_slice_7_zo),
    .co(pin_slice_6_co), .qo(pin_slice_6_qo), .wo(pin_slice_6_wo));
  pin_slice pin_slice_7 (
    .ci(pin_slice_2_co), .qi(pin_slice_2_qo), .zo(pin_slice_7_zo), .wi(pin_slice_8_wo), .zi(pin_slice_2_zo),
    .co(pin_slice_7_co), .qo(pin_slice_7_qo), .wo(pin_slice_7_wo));
  pin_slice pin_slice_8 (
    .ci(pin_slice_3_co), .qi(pin_slice_3_qo), .zo(pin_slice_8_zo), .wi(W1), .zi(pin_slice_3_zo),
    .co(pin_slice_8_co), .qo(pin_slice_8_qo), .wo(pin_slice_8_wo));
  pin_slice pin_slice_9 (
    .ci(pin_slice_8_co), .qi(pin_slice_8_qo), .zo(Z2), .wi(W2), .zi(pin_slice_8_zo), .co(pin_slice_9_co),
    .qo(pin_slice_9_qo), .wo(pin_slice_9_wo));
endmodule

module shift (
  input  SI,
  input  SCLK,
  input  LD,
  input  Z0,
  input  Z1,
  input  Z2,
  output W0,
  output W1,
  output W2,
  output SO
);

  wire shift_slice_1_ldo, shift_slice_1_sclko, shift_slice_1_so, shift_slice_2_ldo, shift_slice_2_sclko,
       shift_slice_2_so;

  shift_slice shift_slice_1 (
    .SCLKI(SCLK), .LDI(LD), .Z(Z0), .SI(SI), .SCLKO(shift_slice_1_sclko), .LDO(shift_slice_1_ldo),
    .SO(shift_slice_1_so), .W(W0));
  shift_slice shift_slice_2 (
    .SCLKI(shift_slice_1_sclko), .LDI(shift_slice_1_ldo), .Z(Z1), .SI(shift_slice_1_so),
    .SCLKO(shift_slice_2_sclko), .LDO(shift_slice_2_ldo), .SO(shift_slice_2_so), .W(W1));
  shift_slice shift_slice_3 (
    .SCLKI(shift_slice_2_sclko), .LDI(shift_slice_2_ldo), .Z(Z2), .SI(shift_slice_2_so), .SO(SO), .W(W2));  // open: SCLKO, LDO
endmodule

module top_internal (
  input  PSI,
  input  SI,
  input  LD,
  output SO
);

  wire PCLK_out, pin_slice_1_co, pin_slice_1_qo, pin_slice_1_zo, pin_slice_2_co, pin_slice_2_qo,
       pin_slice_2_wo, pin_slice_2_zo, pin_slice_3_co, pin_slice_3_qo, pin_slice_3_wo, pin_slice_3_zo,
       pin_slice_4_co, pin_slice_4_qo, pin_slice_4_zo, pin_slice_5_co, pin_slice_5_qo, pin_slice_5_wo,
       pin_slice_5_zo, pin_slice_6_co, pin_slice_6_qo, pin_slice_6_wo, pin_slice_6_zo, pin_slice_7_zo,
       pin_slice_8_co, pin_slice_8_qo, pin_slice_8_wo, pin_slice_8_zo, pin_slice_9_co, pin_slice_9_qo,
       pin_slice_9_wo, pin_slice_9_zo, SCLK_out, shift_slice_1_ldo, shift_slice_1_sclko, shift_slice_1_so,
       shift_slice_1_w, shift_slice_2_ldo, shift_slice_2_sclko, shift_slice_2_so, shift_slice_2_w,
       shift_slice_3_w;

  Button PCLK (.out(PCLK_out));
  Button SCLK (.out(SCLK_out));
  pin_slice pin_slice_1 (
    .ci(pin_slice_8_co), .qi(pin_slice_8_qo), .zo(pin_slice_1_zo), .wi(pin_slice_2_wo), .zi(1'b0),
    .co(pin_slice_1_co), .qo(pin_slice_1_qo));  // open: wo
  pin_slice pin_slice_2 (
    .ci(pin_slice_9_co), .qi(pin_slice_9_qo), .zo(pin_slice_2_zo), .wi(pin_slice_3_wo), .zi(1'b0),
    .co(pin_slice_2_co), .qo(pin_slice_2_qo), .wo(pin_slice_2_wo));
  pin_slice pin_slice_3 (
    .ci(PCLK_out), .qi(PSI), .zo(pin_slice_3_zo), .wi(shift_slice_1_w), .zi(1'b0), .co(pin_slice_3_co),
    .qo(pin_slice_3_qo), .wo(pin_slice_3_wo));
  shift_slice shift_slice_1 (
    .SCLKI(SCLK_out), .LDI(LD), .Z(pin_slice_7_zo), .SI(SI), .SCLKO(shift_slice_1_sclko),
    .LDO(shift_slice_1_ldo), .SO(shift_slice_1_so), .W(shift_slice_1_w));
  pin_slice pin_slice_4 (
    .ci(pin_slice_1_co), .qi(pin_slice_1_qo), .zo(pin_slice_4_zo), .wi(pin_slice_5_wo), .zi(pin_slice_1_zo),
    .co(pin_slice_4_co), .qo(pin_slice_4_qo));  // open: wo
  pin_slice pin_slice_5 (
    .ci(pin_slice_2_co), .qi(pin_slice_2_qo), .zo(pin_slice_5_zo), .wi(pin_slice_6_wo), .zi(pin_slice_2_zo),
    .co(pin_slice_5_co), .qo(pin_slice_5_qo), .wo(pin_slice_5_wo));
  pin_slice pin_slice_6 (
    .ci(pin_slice_3_co), .qi(pin_slice_3_qo), .zo(pin_slice_6_zo), .wi(shift_slice_2_w), .zi(pin_slice_3_zo),
    .co(pin_slice_6_co), .qo(pin_slice_6_qo), .wo(pin_slice_6_wo));
  shift_slice shift_slice_2 (
    .SCLKI(shift_slice_1_sclko), .LDI(shift_slice_1_ldo), .Z(pin_slice_8_zo), .SI(shift_slice_1_so),
    .SCLKO(shift_slice_2_sclko), .LDO(shift_slice_2_ldo), .SO(shift_slice_2_so), .W(shift_slice_2_w));
  pin_slice pin_slice_7 (
    .ci(pin_slice_4_co), .qi(pin_slice_4_qo), .zo(pin_slice_7_zo), .wi(pin_slice_8_wo), .zi(pin_slice_4_zo));  // open: co, qo, wo
  pin_slice pin_slice_8 (
    .ci(pin_slice_5_co), .qi(pin_slice_5_qo), .zo(pin_slice_8_zo), .wi(pin_slice_9_wo), .zi(pin_slice_5_zo),
    .co(pin_slice_8_co), .qo(pin_slice_8_qo), .wo(pin_slice_8_wo));
  pin_slice pin_slice_9 (
    .ci(pin_slice_6_co), .qi(pin_slice_6_qo), .zo(pin_slice_9_zo), .wi(shift_slice_3_w), .zi(pin_slice_6_zo),
    .co(pin_slice_9_co), .qo(pin_slice_9_qo), .wo(pin_slice_9_wo));
  shift_slice shift_slice_3 (
    .SCLKI(shift_slice_2_sclko), .LDI(shift_slice_2_ldo), .Z(pin_slice_9_zo), .SI(shift_slice_2_so), .SO(SO),
    .W(shift_slice_3_w));  // open: SCLKO, LDO
endmodule

module shift_slice (
  input  SCLKI,
  input  LDI,
  input  Z,
  input  SI,
  output SCLKO,
  output LDO,
  output SO,
  output W
);

  wire multiplexer_1_out;

  Multiplexer #(.disabled(0), .enable("false")) multiplexer_1 (.in0(Z), .in1(SI), .out(multiplexer_1_out), .sel(LDI));
  D_Flip_Flop d_ff_1 (.clk(SCLKI), .D(multiplexer_1_out), .Q(SO));  // open: Qn, preset, en, reset

  assign LDO = LDI;
  assign SCLKO = SCLKI;
  assign W = SO;
endmodule

module top (
  input  PSI,
  input  PCLK,
  input  SI,
  input  SCLK,
  input  LD,
  output SO
);

  wire pin_1_z0, pin_1_z1, pin_1_z2, shift_1_w0, shift_1_w1, shift_1_w2;

  pin pin_1 (
    .PSI(PSI), .PCLK(PCLK), .Z0(pin_1_z0), .Z1(pin_1_z1), .Z2(pin_1_z2), .W0(shift_1_w0), .W1(shift_1_w1),
    .W2(shift_1_w2));
  shift shift_1 (
    .SI(SI), .SCLK(SCLK), .LD(LD), .SO(SO), .W0(shift_1_w0), .W1(shift_1_w1), .W2(shift_1_w2), .Z0(pin_1_z0),
    .Z1(pin_1_z1), .Z2(pin_1_z2));
endmodule
